# Fritzing sketch HitagiExpansionBoard (saved by Fritzing 0.9.5d)
circuit board: 10.5cm x 13.5033cm
breadboards: 1

parts:
  MCP23S17 = MCP23S17 [part_number=MCP23S17 package="DIP (Dual Inline) [THT]"]
  LCD1 = Basic 16x2 Character LCD - RGB Backlight 5V [part_number=LCD-10862]
  R2 = Resistor [tolerance=±5% resistance=330 package="0805 [SMD]"]
  R3 = Resistor [tolerance=±5% resistance=330 package="0805 [SMD]"]
  R4 = Resistor [tolerance=±5% resistance=330 package="0805 [SMD]"]
  C1 = Ceramic Capacitor [capacitance=0.1µF voltage=50V package="0805 [SMD, multilayer]"]
  Contrast = TRIMPOT [package=trimpot-3mm]
  SparkFun_Pro_Micro_5v = SparkFun Pro Micro [part_number=DEV-12640]
  STEMMA = female pin header, 4 pins [form="♀ (female)"]
  IO = male pin header, 5 pins [form="♂ (male)"]
  RESET = Pushbutton [package="[THT]"]
  BAT1 = BC9VPC [package=bc9vpc]
  POWER = Toggle Switch [package=THT]
  23LC1024 = 23LCV1024 [part_number=23LC1024 package="DIP (Dual Inline) [THT]"]
  STEMMA1 = Adafruit Stemma 4 pin header [form="♀ (female)" package=THT]
  STEMMA2 = Adafruit Stemma 4 pin header [form="♀ (female)" package=THT]
  R7 = Resistor [tolerance=±5% resistance=10k package="0805 [SMD]"]
  R5 = Resistor [tolerance=±5% resistance=10k package="0805 [SMD]"]
  R6 = Resistor [tolerance=±5% resistance=10k package="0805 [SMD]"]
  STEMMA3 = Adafruit Stemma 4 pin header [form="♀ (female)" package=THT]
  PWM(10) = female pin header, 3 pins [form="♀ (female)"]
  SPI0 = JST PH SPI HEADER [form="♀ (female)" package=THT]
  SPI1 = JST PH SPI HEADER [form="♀ (female)" package=THT]
  SPI2 = JST PH SPI HEADER [form="♀ (female)" package=THT]
  74HC1 = 74HC138 [part_number=SN74HC138DBR package=SSOP-16]
  C3 = Ceramic Capacitor [capacitance=0.1µF voltage=50V package="0805 [SMD, multilayer]"]
  IO1 = male pin header, 4 pins [form="♂ (male)"]
  D7 = female pin header, 3 pins [form="♀ (female)"]
  4/A6 = female pin header, 3 pins [form="♀ (female)"]
  RX/TX = female pin header, 2 pins [form="♀ (female)"]
  8/A8 = female pin header, 3 pins [form="♀ (female)"]
  C2 = Ceramic Capacitor [capacitance=0.1µF voltage=50V package="0805 [SMD, multilayer]"]

nets:
  P0: MCP23S17.GPB0, IO.pin1
  P1: MCP23S17.GPB1, IO.pin2
  P2: MCP23S17.GPB2, IO.pin3
  P3: MCP23S17.GPB3, IO.pin4
  P4: MCP23S17.GPB4, IO1.pin1
  P5: MCP23S17.GPB5, IO1.pin2
  P6: MCP23S17.GPB6, IO1.pin3
  P7: MCP23S17.GPB7, IO1.pin4
  23LC1024 VCC/5V/MCP23S17_VCC/SPI Decoder VCC: MCP23S17.VDD, LCD1.VDD, C1.1, Contrast.CW, SparkFun_Pro_Micro_5v.VCC, STEMMA.pin2, 23LC1024.VCC, STEMMA1.V+, STEMMA2.V+, R7.Pin_0, R5.Pin_0, R6.Pin_0, STEMMA3.V+, PWM(10).pin2, SPI0.VCC, SPI1.VCC, SPI2.VCC, 74HC1.G1, 74HC1.VCC, C3.1, D7.pin2, 4/A6.pin2, 8/A8.pin2, C2.1
  23LC1024 GND/GND/MCP23S17_GND/SPI Decoder GND: MCP23S17.VSS, MCP23S17.A0, MCP23S17.A1, MCP23S17.A2, LCD1.VSS, LCD1.LED-, C1.0, Contrast.CCW, SparkFun_Pro_Micro_5v.GND, STEMMA.pin1, RESET.Pin_3, RESET.Pin_4, BAT1.V-, 23LC1024.VSS, STEMMA1.GND, STEMMA2.GND, STEMMA3.GND, PWM(10).pin1, SPI0.GND, SPI1.GND, SPI2.GND, 74HC1.G2B_, 74HC1.GND, C3.0, D7.pin1, 4/A6.pin1, 8/A8.pin1, C2.0
  MCP23S17 ENABLE: MCP23S17.CS_, 74HC1.Y7
  SCK: MCP23S17.SCK, SparkFun_Pro_Micro_5v.SCK, 23LC1024.SCK, SPI0.SCK, SPI1.SCK, SPI2.SCK
  MOSI: MCP23S17.SI, SparkFun_Pro_Micro_5v.MOSI, 23LC1024.SI/SIO0, SPI0.MOSI, SPI1.MOSI, SPI2.MOSI
  MISO: MCP23S17.SO, SparkFun_Pro_Micro_5v.MISO, 23LC1024.SO/SIO1, SPI0.MISO, SPI1.MISO, SPI2.MISO
  RESET: MCP23S17.RESET_, SparkFun_Pro_Micro_5v.RESET, RESET.Pin_1, RESET.Pin_2
  A7: MCP23S17.GPA0, LCD1.D7
  A6: MCP23S17.GPA1, LCD1.D6
  A5: MCP23S17.GPA2, LCD1.D5
  A4: MCP23S17.GPA3, LCD1.D4
  E: MCP23S17.GPA4, LCD1.E
  RW: MCP23S17.GPA5, LCD1.R/W
  RS: MCP23S17.GPA6, LCD1.RS
  P8: MCP23S17.GPA7, IO.pin5
  CONTRAST: LCD1.Contrast, Contrast.WIPER
  N1: LCD1.RED_LED, R2.Pin_0
  N2: LCD1.GREEN_LED, R3.Pin_0
  N3: LCD1.BLUE_LED, R4.Pin_0
  RED PWM: R2.Pin_1, SparkFun_Pro_Micro_5v.D5
  GREEN PWM: R3.Pin_1, SparkFun_Pro_Micro_5v.D6
  BLUE PWM: R4.Pin_1, SparkFun_Pro_Micro_5v.D9
  9V: SparkFun_Pro_Micro_5v.RAW, POWER.COM
  A3: SparkFun_Pro_Micro_5v.A3, 74HC1.A
  A2: SparkFun_Pro_Micro_5v.A2, 74HC1.B
  A1: SparkFun_Pro_Micro_5v.A1, 74HC1.C
  A0: SparkFun_Pro_Micro_5v.A0, 74HC1.G2A_
  PWM0: SparkFun_Pro_Micro_5v.D10, PWM(10).pin3
  D8: SparkFun_Pro_Micro_5v.D8, 8/A8.pin3
  D7: SparkFun_Pro_Micro_5v.D7, D7.pin3
  D4: SparkFun_Pro_Micro_5v.D4, 4/A6.pin3
  SCL: SparkFun_Pro_Micro_5v.D3, STEMMA.pin4, STEMMA1.SCL, STEMMA2.SCL, STEMMA3.SCL
  SDA: SparkFun_Pro_Micro_5v.D2, STEMMA.pin3, STEMMA1.SDA, STEMMA2.SDA, STEMMA3.SDA
  RXI: SparkFun_Pro_Micro_5v.RXI, RX/TX.pin2
  TXO: SparkFun_Pro_Micro_5v.TXO, RX/TX.pin1
  9V IN: BAT1.V+, POWER.L1
  SRAM Enable: 23LC1024.CS_, R7.Pin_1, 74HC1.Y6
  N4: 23LC1024.NC, R5.Pin_1
  N5: 23LC1024.VBAT, R6.Pin_1
  SPI0 Enable: SPI0.CS_, 74HC1.Y0
  SPI1 Enable: SPI1.CS_, 74HC1.Y1
  SPI2 Enable: SPI2.CS_, 74HC1.Y2

notes:
  REV 2
  "Hitagi" Expansion Board
  (C) 2020 Joshua Scoggins

custom parts:
  MCP23S17: 28-pin DIP Package version of the MCP23S17 16-bit I/O Expander with SPI Interface
  Basic 16x2 Character LCD - RGB Backlight 5V: This is similar to other 16x2 character LCDs that you've seen before but with one vibrant difference: The backlight is actually an RGB LED. This means that you can change the backlight of this display to any color you want by controlling the three backlight levels. It also utilizes an extremely common parallel interface so code is freely available (check below for an Arduino example). You will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
  SparkFun Pro Micro: This tiny little board does all of the neat-o Arduino tricks that you’re familiar with: 4 channels of 10-bit ADC, 5 PWM pins, 12 DIOs as well as hardware serial connections Rx and Tx. Running at 16MHz and 5V, this board will remind you a lot of your other favorite Arduino-compatible boards but this little guy can go just about anywhere. There is a voltage regulator on board so it can accept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
  Adafruit Stemma 4 pin header: Adafruit STEMMA 4 pin header JST PH 4
  JST PH SPI HEADER: Single device JST PH Based SPI Header
  74HC138: 3-to-8 Decoder/Demultiplexer
